# Fritzing sketch nrf24L01 led alıcı (saved by Fritzing 0.9.3b)
breadboards: 2

parts:
  U1 = atmega328 [package=dip]
  U2 = TTL UART CP2102
  2x_22_pF = Capacitor [part_number="(code 22 or 220)" package=cap-pth-small2]
  22pF1 = Capacitor [package=cap-pth-small2]
  0_10_uF = Capacitor [part_number="(code 104)" package=cap-pth-small2]
  Parça2 = NRF24L01+ Breakout Board
  16MHZ = CRYSTAL [part_number=crystal package=hc49u-v]
  R1 = Resistor [tolerance=±5% resistance=10k part_number=resistor package=THT]
  C1 = Capacitor Polarized [package=cpol-radial-100uf-25v]
  LED1 = LEDs [package=led10mm]
  LED2 = LEDs [package=led10mm]
  R2 = Resistor [tolerance=±5% resistance=220 package="2010 [SMD]"]
  R3 = Resistor [tolerance=±5% resistance=220 package="1206 [SMD]"]

nets:
  GND: U1.D0_(RX), U1.D6_(PWM), U1.D11_(PWM), U2.GND, 2x_22_pF.1, 22pF1.2, Parça2.GND, C1.-, LED1.C, LED2.C
  N1: U1.D1_(TX), U1.D7
  N2: U1.D2, 22pF1.1, 16MHZ.2
  N3: U1.D9_(PWM), 0_10_uF.2, R1.Pin_0
  N4: U1.D10_(PWM), U1.A3
  +5V: U1.A4, U2.+5V, Parça2.VCC, R1.Pin_1, C1.+
  N5: U2.DTR, 0_10_uF.1
  N6: 2x_22_pF.2, 16MHZ.1
  N7: LED1.A, R2.Pin_1
  N8: LED2.A, R3.Pin_1

custom parts:
  TTL UART CP2102: 6Pin USB 2.0 to TTL UART Module Serial Converter CP2102 STC Replace Ft232 Module
